# Fritzing sketch Head-Board (saved by Fritzing 0.9.3b)
circuit board: 10cm x 7cm
breadboards: 1

parts:
  Composant1 = Arduino Nano (Rev3.0)
  Y = Pololu A4988 [package=SO16]
  Z = Pololu A4988 [package=SO16]
  X = Pololu A4988 [package=SO16]
  J1 = Screw terminal - 2 pins [package=THT]
  J2 = Screw terminal - 2 pins [package=THT]
  J3 = Screw terminal - 2 pins [package=THT]
  J4 = Screw terminal - 2 pins [package=THT]
  J5 = Screw terminal - 2 pins [package=THT]
  C1 = Electrolytic Capacitor [capacitance=1µF package="100 mil [THT, electrolytic]"]
  C2 = Electrolytic Capacitor [capacitance=1µF package="100 mil [THT, electrolytic]"]
  C3 = Electrolytic Capacitor [capacitance=1µF package="100 mil [THT, electrolytic]"]
  J6 = Screw terminal - 2 pins [package=THT]
  J7 = Screw terminal - 2 pins [package=THT]
  J8 = Screw terminal - 2 pins [package=THT]
  J9 = Screw terminal - 2 pins [package=THT]
  R1 = Resistor [tolerance=±5% resistance=220 package=THT]
  R2 = Resistor [tolerance=±5% resistance=220 package=THT]
  R3 = Resistor [tolerance=±5% resistance=220 package=THT]
  R4 = Resistor [tolerance=±5% resistance=220 package=THT]
  LED1 = LED - 3mm [color="Blue (505nm)" package="3 mm [THT]"]
  LED4 = LED - 3mm [color="Red (633nm)" package="3 mm [THT]"]
  LED3 = LED - 3mm [color="Blue (505nm)" package="3 mm [THT]"]
  LED5 = LED - 3mm [color="Red (633nm)" package="3 mm [THT]"]
  R5 = Resistor [tolerance=±5% resistance=220 package=THT]
  LED2 = LED - 3mm [color="Blue (505nm)" package="3 mm [THT]"]
  LED6 = LED - 3mm [color="Red (633nm)" package="3 mm [THT]"]
  R6 = Resistor [tolerance=±5% resistance=220 package=THT]
  J12 = female pin header, 3 pins [form="♀ (female)"]

nets:
  GND: Composant1.GND, Y.GND, Z.GND, X.GND, J1.pin2, C1.-, C3.-, J9.pin2, LED1.cathode, LED4.cathode, LED3.cathode, LED5.cathode, J12.pin1
  N1: Composant1.D2, Z.DIR
  N2: Composant1.D3, Z.STEP
  N3: Composant1.D4, Z.ENABLE
  N4: Composant1.D5, X.DIR
  N5: Composant1.D6, X.STEP
  N6: Composant1.D7, X.ENABLE
  N7: Composant1.D8, Y.DIR
  N8: Composant1.D9, Y.STEP
  N9: Composant1.D10, Y.ENABLE
  VDD: Composant1.5V, Y.VDD, Z.VDD, X.VDD, J9.pin1, J12.pin3
  N10: Composant1.A5, J8.pin2
  N11: Composant1.A4, J8.pin1
  N12: Composant1.AREF, J12.pin2
  N13: Y.RESET, Y.SLEEP
  N14: Y.1B, J3.pin2
  N15: Y.1A, J3.pin1
  N16: Y.2A, J2.pin2
  N17: Y.2B, J2.pin1
  N18: Y.VMOT, Z.VMOT, X.VMOT, J1.pin1, C1.+, C2.+, C3.+
  N19: Z.RESET, Z.SLEEP
  N20: Z.1B, J7.pin2
  N21: Z.1A, J7.pin1
  N22: Z.2A, J6.pin2
  N23: Z.2B, J6.pin1
  N24: X.RESET, X.SLEEP
  N25: X.1B, J5.pin2
  N26: X.1A, J5.pin1
  N27: X.2A, J4.pin2
  N28: X.2B, J4.pin1
  N29: R1.Pin_0, LED3.anode
  N30: R2.Pin_1, LED2.anode
  N31: R3.Pin_0, LED1.anode
  N32: R4.Pin_0, LED4.anode
  N33: LED5.anode, R5.Pin_0
  N34: LED6.anode, R6.Pin_1

notes:
  BB-8 HEAD DRIVE V1
  GITHUB/Gruniek/OPEN-BB-X
